# Fritzing sketch Вжух (saved by Fritzing 0.9.3b)
circuit board: 3.88803cm x 3.03231cm
breadboards: 1

parts:
  M1 = DC Motor
  M2 = DC Motor
  IC1 = IC, DIP package, 8 pins [chip_label=IC]
  Q1 = NPN-Transistor [package="TO92 [THT]"]
  Q2 = NPN-Transistor [package="TO92 [THT]"]
  D1 = Rectifier Diode [part_number=1N4001 package="300 mil [THT]"]
  D2 = Rectifier Diode [part_number=1N4001 package="300 mil [THT]"]
  U1 = Voltage Regulator - 5V [package="TO220 [THT]"]
  VCC1 = Battery block 9V
  J1 = female pin header, 10 pins [form="♀ (female)"]
  C1 = Electrolytic Capacitor [capacitance=1µF package="100 mil [THT, electrolytic]"]
  C2 = Electrolytic Capacitor [capacitance=1µF package="100 mil [THT, electrolytic]"]

nets:
  N1: M1.pin_1, Q1.C, D1.cathode
  N2: M1.pin_2, M2.pin_2, D1.anode, D2.anode, U1.input_voltage, VCC1.+, C1.+
  N3: M2.pin_1, Q2.C, D2.cathode
  N4: IC1.pin2, Q2.B
  N5: IC1.pin3, J1.pin2
  N6: IC1.pin4, Q1.E, Q2.E, U1.GND, VCC1.-, J1.pin1, J1.pin5, J1.pin8, C1.-, C2.-
  N7: IC1.pin5, J1.pin6
  N8: IC1.pin6, J1.pin9
  N9: IC1.pin7, Q1.B
  N10: IC1.pin8, U1.output_voltage, J1.pin3, J1.pin7, J1.pin10, C2.+
