# Fritzing sketch Вжух2 (saved by Fritzing 0.9.3b)
circuit board: 4.41615cm x 3.87326cm
breadboards: 1

parts:
  U1 = Voltage Regulator - 5V [package="TO220 [THT]"]
  VCC1 = Battery
  U2 = ATTINY45 [package=dip]
  J3 = Screw terminal - 2 pins [package=THT]
  C1 = Electrolytic Capacitor [capacitance=1µF package="100 mil [THT, electrolytic]"]
  J1 = male pin header, 10 pins [form="♂ (male)"]
  Q1 = Basic FET N-Channel [package="TO220 [THT]"]
  Q2 = Basic FET N-Channel [package="TO220 [THT]"]
  C2 = Electrolytic Capacitor [capacitance=1µF package="100 mil [THT, electrolytic]"]
  D1 = Diode [package=diode-hv]
  D2 = Diode [package=diode-hv]
  J2 = Screw terminal - 2 pins [package=THT]

nets:
  N1: U1.input_voltage, VCC1.+, C1.-, Q1.gate, Q2.gate
  GND: U1.GND, VCC1.-, U2.GND, J3.pin1, C1.+, J1.pin3, J1.pin6, J1.pin9, C2.+, D1.A, D2.A, J2.pin1
  N2: U1.output_voltage, U2.VCC, J1.pin1, J1.pin4, J1.pin7, C2.-
  N3: U2.PB3(ADC3), J1.pin5
  N4: U2.PB4(ADC2), J1.pin8
  N5: U2.PB0(MOSI), Q2.drain
  N6: U2.PB1(MISO), Q1.drain
  N7: U2.PB2(SCK_ADC1), J1.pin2
  N8: J3.pin2, Q2.source, D1.C
  N9: Q1.source, D2.C, J2.pin2
